# Fritzing sketch arduino (saved by Fritzing 0.9.3b)
breadboards: 1

parts:
  부품1 = FC-28 Soil Hygrometer Module - Probe
  부품2 = FC-28 Soil Hygrometer Module
  부품3 = Arduino Uno (Rev3)
  WATER_PUMP1 = water pump/motor
  KF-1 = KF-301 Relay [package=THT]
  BAT1 = 18650 battery holder [package=battery-18650-kit]
  BAT2 = 18650 battery holder [package=battery-18650-kit]
  U1 = ESP8266 WiFi Module [part_number=ESP8266]
  부품4 = FC-28 Soil Hygrometer Module - Probe
  부품5 = FC-28 Soil Hygrometer Module
  부품6 = FC-28 Soil Hygrometer Module - Probe
  부품7 = FC-28 Soil Hygrometer Module

nets:
  N1: 부품1.POS, 부품2.POS
  N2: 부품1.NEG, 부품2.NEG
  VCC: 부품2.VCC, 부품3.5V, KF-1.power, 부품5.VCC
  GND: 부품2.GND, 부품3.GND, KF-1.ground, U1.GND, 부품5.GND
  N3: 부품2.AO, 부품3.A5/SCL
  N4: 부품3.A3, 부품5.AO
  N5: 부품3.A4/SDA, 부품7.AO
  N6: 부품3.D0/RX, U1.TXD
  N7: 부품3.D1/TX, U1.RXD
  N8: 부품3.D2, KF-1.signal
  3V3: 부품3.3V3, U1.VCC
  N9: WATER_PUMP1.pin_1, BAT1.+
  N10: WATER_PUMP1.pin_2, KF-1.C
  N11: KF-1.NO, BAT2.-
  N12: 부품4.POS, 부품5.POS
  N13: 부품4.NEG, 부품5.NEG
  N14: 부품6.POS, 부품7.POS
  N15: 부품6.NEG, 부품7.NEG

custom parts:
  FC-28 Soil Hygrometer Module - Probe: The FC-28 is a soil hygrometer module that uses the Texas Instruments LM393 comparator chip to provide an analog measurement of soil humidity.
  FC-28 Soil Hygrometer Module: The FC-28 is a soil hygrometer module that uses the Texas Instruments LM393 comparator chip to provide an analog measurement of soil humidity. The digital output is high when soil moisture is over a certain threshold, as determined by adjusting the potentiometer.
  water pump/motor: WATER PUMP BY ARDUBLOCKTR
  KF-301 Relay: KF-301
  18650 battery holder: 18650 Battery Holder identical to the dual battery version.
  ESP8266 WiFi Module: Generic WiFi Module based on the ESP8266 with onboard PCB antenna and UART communications
