# Fritzing sketch raspberry_pi_wiring (saved by Fritzing 0.9.3b)

parts:
  Raspberry_Pi_1 = Raspberry Pi 3 [part_number=RPI-3-V1.2]
  DS1 = DS18B20 1-Wire Temperature Sensor [part_number=DS18B20]

nets:
  3V3: Raspberry_Pi_1.3v3, DS1.VDD
  N1: Raspberry_Pi_1.GIPO4, DS1.DQ
  GND: Raspberry_Pi_1.GND, DS1.GND
